# Fritzing sketch light_controller (saved by Fritzing 0.9.2b)
circuit board: 6.88566cm x 5.36311cm
breadboards: 2

parts:
  Q1 = MOSFET-NCHANNEL [package=to220v]
  Part1 = Arduino Uno (Rev3) - ICSP
  IR1 = TSOP312.., 314.. [package=THT]
  R1 = Resistor [tolerance=±5% resistance=120 package=THT]
  R4 = Resistor [tolerance=±5% resistance=10k package=THT]
  Q2 = MOSFET-NCHANNEL [package=to220v]
  Q3 = MOSFET-NCHANNEL [package=to220v]
  R5 = Resistor [tolerance=±5% resistance=10k package=THT]
  R6 = Resistor [tolerance=±5% resistance=10k package=THT]

nets:
  N1: Q1.G, Part1.D5_PWM, R4.Pin_0
  N2: Q1.S, Part1.GND, IR1.Vs, R4.Pin_1, Q2.S, Q3.S, R5.Pin_1, R6.Pin_1
  N3: Part1.ICSP_MOSI, Part1.D11_PWM/MOSI, IR1.GND
  N4: Part1.RESET, R1.Pin_0
  N5: Part1.5V, IR1.Data, R1.Pin_1
  N6: Part1.D9_PWM, Q2.G, R5.Pin_0
  N7: Part1.D10_PWM/SS, Q3.G, R6.Pin_0
